# Fritzing sketch AlexaBridge (saved by Fritzing 0.9.3b)
circuit board: 7.6cm x 8.8cm
breadboards: 2

parts:
  U1 = ESP32-38PinWide [part_number=ESP32-38PinWide]
  Microphone = INMP441
  Buck_Converter = SBX DSUN [package=THT]
  GND_12V = Screw terminal - 2 pins [package=THT]
  Wifi_Reset = Pushbutton [package="[THT]"]
  VCC1 = Battery block 9V
  10k = Resistor [tolerance=±2% resistance=1k package=THT]
  UDN2981 = IC, DIP package, 18 pins [chip_label=IC]
  26_27 = Screw terminal - 2 pins [package=THT]
  33_25 = screw terminal, 2 pins
  GND_GND = Screw terminal - 2 pins [package=THT]
  Pin13 = female pin header, 1 pin [form="♀ (female)"]
  UDN2981_2 = IC, DIP package, 18 pins [chip_label=IC]
  17_16 = Screw terminal - 2 pins [package=THT]
  18_05 = screw terminal, 2 pins
  GND_19 = Screw terminal - 2 pins [package=THT]
  Relais_12V = srd-05vdc-sl-c
  FOG = Screw terminal - 2 pins [package=THT]

nets:
  N1: U1.3.3, Microphone.VDD, Wifi_Reset.Pin_1, Wifi_Reset.Pin_2
  N2: U1.GPIO32, UDN2981.pin5
  N3: U1.GPIO33, UDN2981.pin4
  N4: U1.GPIO25, UDN2981.pin3
  N5: U1.GPIO26, UDN2981.pin2
  N6: U1.GPIO27, UDN2981.pin1
  GND: U1.GND, Microphone.L/R, Microphone.GND, Buck_Converter.GND, GND_12V.pin1, VCC1.-, 10k.Pin_0, UDN2981.pin10, GND_GND.pin1, GND_GND.pin2, UDN2981_2.pin10, GND_19.pin2, Relais_12V.pin_1
  N7: U1.GPIO13, Pin13.pin1
  N8: U1.VIN, Buck_Converter.+VOUT
  N9: U1.GPIO4, Wifi_Reset.Pin_3, Wifi_Reset.Pin_4, 10k.Pin_1
  N10: U1.GPIO16, UDN2981_2.pin1
  N11: U1.GPIO17, UDN2981_2.pin2
  N12: U1.GPIO5, UDN2981_2.pin3
  N13: U1.GPIO18, UDN2981_2.pin4
  N14: U1.GPIO19, UDN2981_2.pin5
  N15: U1.GPIO21, Microphone.SD
  N16: U1.GPIO22, Microphone.SCK
  N17: U1.GPIO23, Microphone.WS
  N18: Buck_Converter.+VIN, GND_12V.pin2, VCC1.+, UDN2981.pin9, UDN2981_2.pin9
  N19: UDN2981.pin14, Relais_12V.pin_4
  N20: UDN2981.pin15, 33_25.pin2
  N21: UDN2981.pin16, 33_25.pin1
  N22: UDN2981.pin17, 26_27.pin2
  N23: UDN2981.pin18, 26_27.pin1
  N24: UDN2981_2.pin14, GND_19.pin1
  N25: UDN2981_2.pin15, 18_05.pin2
  N26: UDN2981_2.pin16, 18_05.pin1
  N27: UDN2981_2.pin17, 17_16.pin2
  N28: UDN2981_2.pin18, 17_16.pin1
  N29: Relais_12V.pin_2, FOG.pin1
  N30: Relais_12V.pin_5, FOG.pin2

custom parts:
  ESP32-38PinWide: Generic 38-Pin ESP32 with wide format (only access to one side of pins on a breadboard) based on Stephen Lilley's HiLetgo ESP-WROOM-32 ESP32 ESP-32S Development Board.
  INMP441: This is a simple breakout board for the INMP441 I2S MEMS microphone.
  SBX DSUN: SBX DSUN input voltage 4.5 - 28V DC output voltage .8v to 20VDC (step down converter) Output current 3A max
